# Fritzing sketch Ardiuno-Ultrasonic (saved by Fritzing 0.9.3b)

parts:
  Part1 = Arduino Uno (Rev3) - ICSP
  hc-sr1 = hc-sr04

nets:
  N1: Part1.D6_PWM, hc-sr1.Trig
  N2: Part1.D7, hc-sr1.Echo
  5V: Part1.5V, hc-sr1.VCC
  GND: Part1.GND, hc-sr1.GND
